# Fritzing sketch Wemos_2_Buttons (saved by Fritzing 0.9.9b)
breadboards: 1

parts:
  WeMos_D1_Mini1 = WeMos D1 Mini  # not connected
  S1 = Pushbutton [package="[THT]"]
  S2 = Pushbutton [package="[THT]"]

nets:
  N1: S1.Pin_1, S1.Pin_2, S2.Pin_1, S2.Pin_2
  N2: S1.Pin_3, S1.Pin_4
  N3: S2.Pin_3, S2.Pin_4
